// Logisim project lab10B.circ as structural Verilog: 2 circuits, main circuit main
module main (
  input  WriteEnable,
  input  [1:0] ReadRegister1,
  input  [1:0] ReadRegister2,
  input  [1:0] WriteRegister,
  input  [15:0] WriteData,
  input  Clock,
  output [15:0] ReadData1,
  output [15:0] ReadData2
);

  wire demultiplexer_1_out0, demultiplexer_1_out1, demultiplexer_1_out2, demultiplexer_1_out3;
  wire [15:0] register_1_q, register_2_q, register_3_q, register_4_q;

  Demultiplexer #(.select(2)) demultiplexer_1 (
    .out0(demultiplexer_1_out0), .out1(demultiplexer_1_out1), .out2(demultiplexer_1_out2),
    .out3(demultiplexer_1_out3), .in(WriteEnable), .sel(WriteRegister));  // open: en
  Register #(.width(16)) register_1 (
    .D(WriteData), .en(demultiplexer_1_out0), .Q(register_1_q), .clk(Clock));  // open: clr
  Register #(.width(16)) register_2 (
    .D(WriteData), .en(demultiplexer_1_out1), .Q(register_2_q), .clk(Clock));  // open: clr
  Register #(.width(16)) register_3 (
    .D(WriteData), .en(demultiplexer_1_out2), .Q(register_3_q), .clk(Clock));  // open: clr
  Register #(.width(16)) register_4 (
    .D(WriteData), .en(demultiplexer_1_out3), .Q(register_4_q), .clk(Clock));  // open: clr
  Multiplexer #(.select(2), .width(16)) multiplexer_1 (
    .in0(register_1_q), .in1(register_2_q), .in2(register_3_q), .in3(register_4_q), .out(ReadData1),
    .sel(ReadRegister1));  // open: en
  Multiplexer #(.select(2), .width(16), .disabled(0)) multiplexer_2 (
    .in0(register_1_q), .in1(register_2_q), .in2(register_3_q), .in3(register_4_q), .out(ReadData2),
    .sel(ReadRegister2));  // open: en

  // Notes on the sheet:
  //   of your circuit.
  //   These are the inputs
  //   Do not modify this!
  //   Put your name and id here: Xirui Ren - xir19
  //   These are the outputs
  //   of your circuit.
  //   Do not modify this!
endmodule

module register_file (
  input  WriteEnable,
  input  [1:0] ReadRegister1,
  input  [1:0] ReadRegister2,
  input  [1:0] WriteRegiter,
  input  [15:0] WriteData,
  input  Clock,
  output [15:0] ReadData1,
  output [15:0] ReadData2
);

  Register #(.width(16)) register_1 (.Q(ReadData1), .clk(Clock));  // open: D, en, clr
  Register #(.width(16)) register_2 (.clk(Clock));  // open: D, en, Q, clr
  Register #(.width(16)) register_3 (.clk(Clock));  // open: D, en, Q, clr
  Register #(.width(16)) register_4 (.Q(ReadData2), .clk(Clock));  // open: D, en, clr
endmodule
