// Logisim project lab11B.circ as structural Verilog: 1 circuit, main circuit main
module main (
  input  clear,
  output sel,
  output ld,
  output [3:0] address,
  output [3:0] data
);

  wire clock_1_out, counter_1_carry, not_1_p2, not_2_p2;
  wire [3:0] counter_1_q, counter_2_q;

  // NOT_Gate not_1: pin names not known; wires that end beside it: ld, not_1_p2
  Counter #(.width(4), .max('hf), .ongoal("stay")) counter_1 (
    .D(counter_1_q), .count(1'b1), .Q(counter_1_q), .carry(counter_1_carry), .clk(clock_1_out), .clr(clear));  // open: load
  assign address = not_1_p2 ? counter_1_q : 4'bz;  // Controlled_Buffer controlled_buffer_1
  Clock clock_1 (.out(clock_1_out));
  D_Flip_Flop d_ff_1 (.clk(clock_1_out), .D(counter_1_carry), .Q(ld), .reset(clear));  // open: Qn, preset, en
  // NOT_Gate not_2: pin names not known; wires that end beside it: ld, not_2_p2
  RAM #(.addrWidth(4), .dataWidth(4)) ram_1 (
    .addr(address), .data(data), .sel(1'b1), .clk(clock_1_out), .ld(ld), .clr(clear));
  assign data = not_2_p2 ? counter_2_q : 4'bz;  // Controlled_Buffer controlled_buffer_2
  Counter #(.width(4), .max('hf)) counter_2 (
    .count(1'b1), .Q(counter_2_q), .clk(clock_1_out), .clr(clear));  // open: load, D, carry

  assign sel = 1'b1;

  // Other names for the same wires on the sheet: clr = clear

  // Notes on the sheet:
  //   These are the inputs
  //   of your circuit.
  //   Do not modify this!
  //   Put your name and id here: Xirui Ren - xir19
  //   These are the outputs
  //   of your circuit.
  //   Do not modify this!
endmodule
