// Logisim project lab12C.circ as structural Verilog: 3 circuits, main circuit main
module main (
  input  Bit,
  input  Clock,
  output Output
);

  wire [1:0] register_1_q, statetrans_1_newstate0;

  Register #(.width(2)) register_1 (.D(statetrans_1_newstate0), .Q(register_1_q), .clk(Clock));  // open: en, clr
  stateTrans statetrans_1 (
    .state0(register_1_q[1]), .state1(register_1_q[0]), .Bit(Bit), .newState1(statetrans_1_newstate0[1]),
    .newState0(statetrans_1_newstate0[0]));
  out out_1 (.state0(register_1_q[1]), .state1(register_1_q[0]), .\output (Output));

  // Notes on the sheet:
  //   of your circuit.
  //   These are the inputs
  //   Do not modify this!
  //   These are the outputs
  //   of your circuit.
  //   Do not modify this!
endmodule

module stateTrans (
  input  state0,
  input  state1,
  input  Bit,
  output newState1,
  output newState0
);

  wire and_1_out, and_2_out, and_3_out, and_4_out, and_5_out, not_1_p2, not_2_p3, not_3_p4, not_4_p3,
       not_5_p3, not_6_p3;

  // NOT_Gate not_1: pin names not known; wires that end beside it: state0, not_1_p2
  // NOT_Gate not_2: pin names not known; wires that end beside it: state1, state0, not_2_p3
  // NOT_Gate not_3: pin names not known; wires that end beside it: state1, state0, state1, not_3_p4
  // NOT_Gate not_4: pin names not known; wires that end beside it: state0, state1, not_4_p3
  // NOT_Gate not_5: pin names not known; wires that end beside it: state1, Bit, not_5_p3
  // NOT_Gate not_6: pin names not known; wires that end beside it: state1, Bit, not_6_p3
  and and_1 (and_1_out, not_1_p2, state1, Bit);
  and and_2 (and_2_out, state0, not_2_p3);
  and and_3 (and_3_out, not_3_p4, not_4_p3, Bit);
  and and_4 (and_4_out, state0, not_5_p3, not_6_p3);
  and and_5 (and_5_out, state0, state1, Bit);
  // OR_Gate or_1: pin names not known; wires that end beside it: and_1_out, and_1_out, and_2_out, newState1
  or or_2 (newState0, and_3_out, and_4_out, and_5_out);
endmodule

module out (
  input  state0,
  input  state1,
  output \output 
);

  and and_1 (\output , state0, state1);
endmodule
