// Logisim project lab8A.circ as structural Verilog: 1 circuit, main circuit main
module main (
  input  A,
  input  B,
  input  C_in,
  output S,
  output C_out
);

  wire A1_out, A2_p3, A3_out, A4_p3, A5_out, A6_out, A7_p3, A7_p4, A9_out, A10_out, A11_out, not_1_p2,
       not_2_p2, not_3_out, O1_out, O2_p4, O4_p3;

  // NOT_Gate not_1: pin names not known; wires that end beside it: A, not_1_p2
  // NOT_Gate not_2: pin names not known; wires that end beside it: B, not_2_p2
  not not_3 (not_3_out, C_in);
  and A1 (A1_out, not_1_p2, not_2_p2);
  // AND_Gate A2: pin names not known; wires that end beside it: not_1_p2, B, A2_p3
  and A3 (A3_out, A, not_2_p2, not_2_p2);
  // AND_Gate A4: pin names not known; wires that end beside it: A, B, A4_p3
  and A5 (A5_out, A1_out, C_in);
  and A6 (A6_out, A2_p3, not_3_out, A3_out);
  // AND_Gate A7: pin names not known; wires that end beside it: A3_out, not_3_out, A7_p3, A7_p4
  and A8 (A7_p4, A4_p3, A4_p3, C_in);
  and A9 (A9_out, A, C_in);
  and A10 (A10_out, C_in, B);
  and A11 (A11_out, A, B);
  or O1 (O1_out, A5_out, A6_out);
  // OR_Gate O2: pin names not known; wires that end beside it: A7_p3, A7_p3, A7_p4, O2_p4
  // OR_Gate O4: pin names not known; wires that end beside it: A9_out, A10_out, O4_p3, A11_out
  or O5 (C_out, O4_p3, O4_p3, A11_out, A11_out);
  or O3 (S, O1_out, O2_p4);

  // Notes on the sheet:
  //   These are the inputs
  //   of your circuit.
  //   Do not modify this!
  //   Put your name and id here: Xirui Ren - xir19
  //   This circuit is wrong :D
  //   Implement here your adder!
  //   These are the outputs
  //   of your circuit.
  //   Do not modify this!
endmodule
