// Logisim project lab8B.circ as structural Verilog: 1 circuit, main circuit main
module main (
  input  A,
  input  B,
  input  C,
  output Q
);

  wire and_1_out, and_2_p3, and_3_out, and_4_p3, and_5_out, and_6_out, and_7_out, and_8_out, and_10_out,
       not_1_out, not_2_p2, not_3_out, or_1_out, or_2_p2, or_2_p3, or_3_p4;

  not not_1 (not_1_out, A);
  // NOT_Gate not_2: pin names not known; wires that end beside it: B, not_2_p2
  not not_3 (not_3_out, C);
  and and_1 (and_1_out, not_1_out, not_1_out, B);
  // AND_Gate and_2: pin names not known; wires that end beside it: A, not_2_p2, and_2_p3
  and and_3 (and_3_out, A, not_2_p2);
  // AND_Gate and_4: pin names not known; wires that end beside it: A, B, and_4_p3
  and and_5 (and_5_out, A, B);
  and and_6 (and_6_out, and_1_out, C);
  or or_1 (or_1_out, and_6_out, and_7_out);
  and and_7 (and_7_out, and_2_p3, not_3_out);
  and and_8 (and_8_out, and_3_out, C);
  // OR_Gate or_2: pin names not known; wires that end beside it: and_8_out, or_2_p2, or_2_p3
  and and_9 (or_2_p2, and_4_p3, not_3_out);
  and and_10 (and_10_out, and_5_out, C);
  // OR_Gate or_3: pin names not known; wires that end beside it: or_2_p3, and_10_out, and_10_out, or_3_p4
  or or_4 (Q, or_1_out, or_3_p4);

  // Notes on the sheet:
  //   of your circuit.
  //   These are the inputs
  //   Do not modify this!
  //   Put your name and id here: Xirui Ren - xir19
  //   These are the outputs
  //   of your circuit.
  //   Do not modify this!
endmodule
