// Logisim project lab9A_grader.circ as structural Verilog: 1 circuit, main circuit main
module main (
  output A,
  output B,
  output C,
  output C_2,
  output Y,
  output halt
);

  wire clock_1_out, comparator_1_eq, main_1_y, not_1_out;
  wire [3:0] counter_1_q;

  Counter #(.width(4), .max('hf)) counter_1 (
    .count(1'b1), .Q(counter_1_q), .carry(halt), .clk(clock_1_out));  // open: load, D, clr
  Clock clock_1 (.out(clock_1_out));
  ROM #(.addrWidth(4), .dataWidth(4)) rom_1 (.addr(counter_1_q), .data({C_2, C, B, A}), .sel(1'b1));
  lab9A_main main_1 (.A_1(A), .A_0(B), .B_1(C), .B_0(C_2), .Y(main_1_y));
  // Probe on {A, B}
  // Probe on {C, C_2}
  assign Y = not_1_out ? main_1_y : 1'bz;  // Controlled_Buffer controlled_buffer_1
  not not_1 (not_1_out, comparator_1_eq);
  Comparator #(.width(2)) comparator_1 (.a({A, B}), .b({C, C_2}), .eq(comparator_1_eq));  // open: gt, lt
  LED led_1 (.in(Y));

  // Other names for the same wires on the sheet: A1 = A; A0 = B; B0 = C_2; B1 = C

  // Notes on the sheet:
  //   contents of rom_1 (hex, n*v repeats v):
  //   0 1 2 3 4 5 6 7 8 9 a b c d e f
  //   When they are the same, we don't care... so I disconnect the circuit :D
endmodule
