// Logisim project lab9B.circ as structural Verilog: 2 circuits, main circuit main
module main (
  input  [3:0] Number
);

  wire d0, d1, d2, d3, d4, d5, d6, d7;

  Solution solution (.Number_to_display(Number), .Segment_configuration({d7, d6, d5, d4, d3, d2, d1, d0}));
  _7_Segment_Display u_7_segment_display_1 (.g(d0), .f(d1), .a(d2), .b(d3), .e(d7), .d(d6), .c(d5), .dp(d4));

  // Notes on the sheet:
  //   This is what the autograder looks like
  //   1. Modify the solution subcircuit
  //   2. Make sure the circuit still connects correctly
  //   Change the number
  //   If you need to modify this circuit, your solution will fail!
  //   Display changes
endmodule

module Solution (
  input  [3:0] Number_to_display,
  output [7:0] Segment_configuration
);

  wire and_1_out, and_2_out, and_3_p3, and_4_out, and_5_out, and_6_out, and_7_p3, and_8_p3, and_9_out,
       and_10_p3, and_11_out, and_12_out, and_13_p3, and_14_out, and_15_p3, and_16_out, and_17_out,
       and_18_p3, and_19_p4, d0, d1, d2, d3, d4, d5, d6, d7, not_1_p2, not_2_out, not_3_p2, not_5_p2,
       not_6_out, not_7_p2, not_9_p2, not_10_out, not_11_p2, not_15_p2, not_16_out, not_21_p2, not_23_p2,
       not_25_p2, not_27_p2, not_30_out, or_1_out, or_2_out, or_3_out, or_4_out, or_5_p4, or_9_out,
       or_10_out, or_11_out, or_15_out, or_16_out, or_17_out;

  // NOT_Gate not_1: pin names not known; wires that end beside it: Number_to_display[0], not_1_p2
  not not_2 (not_2_out, Number_to_display[1]);
  // NOT_Gate not_3: pin names not known; wires that end beside it: Number_to_display[2], not_3_p2
  // NOT_Gate not_4: pin names not known; wires that end beside it: Number_to_display[3]
  // NOT_Gate not_5: pin names not known; wires that end beside it: Number_to_display[0], not_5_p2
  not not_6 (not_6_out, Number_to_display[1]);
  // NOT_Gate not_7: pin names not known; wires that end beside it: Number_to_display[2], not_7_p2
  // NOT_Gate not_8: pin names not known; wires that end beside it: Number_to_display[3]
  // NOT_Gate not_9: pin names not known; wires that end beside it: Number_to_display[0], not_9_p2
  not not_10 (not_10_out, Number_to_display[1]);
  // NOT_Gate not_11: pin names not known; wires that end beside it: Number_to_display[2], not_11_p2
  // NOT_Gate not_12: pin names not known; wires that end beside it: Number_to_display[3]
  and and_1 (and_1_out, not_1_p2, Number_to_display[1]);
  and and_2 (and_2_out, not_2_out, Number_to_display[2]);
  // AND_Gate and_3: pin names not known; wires that end beside it: Number_to_display[1], not_3_p2, and_3_p3
  and and_4 (and_4_out, Number_to_display[0], Number_to_display[1]);
  and and_5 (and_5_out, not_6_out, not_5_p2);
  and and_6 (and_6_out, Number_to_display[0], not_10_out);
  // AND_Gate and_7: pin names not known; wires that end beside it: not_9_p2, not_11_p2, and_7_p3
  // AND_Gate and_8: pin names not known; wires that end beside it: Number_to_display[1], not_9_p2, and_8_p3
  and and_9 (and_9_out, Number_to_display[1], not_11_p2);
  or or_1 (or_1_out, and_1_out, and_2_out);
  or or_2 (or_2_out, and_3_p3, Number_to_display[3]);
  or or_3 (or_3_out, and_4_out, and_5_out);
  // AND_Gate and_10: pin names not known; wires that end beside it: and_6_out, Number_to_display[2], and_10_p3
  or or_4 (or_4_out, and_10_p3, and_7_p3, and_7_p3);
  // OR_Gate or_5: pin names not known; wires that end beside it: and_8_p3, and_8_p3, and_9_out, or_5_p4
  ROM #(.addrWidth(4)) rom_1 (.addr(Number_to_display), .data(Segment_configuration), .sel(1'b1));
  or or_6 (d0, or_1_out, or_2_out);
  // OR_Gate or_7: pin names not known; wires that end beside it: or_3_out, not_7_p2, d3
  or or_8 (d6, or_4_out, or_9_out);
  or or_9 (or_9_out, or_5_p4, Number_to_display[3]);
  // NOT_Gate not_13: pin names not known; wires that end beside it: Number_to_display[0]
  // NOT_Gate not_14 has open pins: in=Number_to_display[1], out=open
  // NOT_Gate not_15: pin names not known; wires that end beside it: Number_to_display[0], not_15_p2
  and and_11 (and_11_out, not_15_p2, not_16_out);
  not not_16 (not_16_out, Number_to_display[1]);
  and and_12 (and_12_out, not_16_out, not_16_out, Number_to_display[2]);
  // AND_Gate and_13: pin names not known; wires that end beside it: not_15_p2, Number_to_display[2], and_13_p3
  // NOT_Gate not_17: pin names not known; wires that end beside it: Number_to_display[2]
  // NOT_Gate not_18: pin names not known; wires that end beside it: Number_to_display[3]
  and and_14 (and_14_out, Number_to_display[3], Number_to_display[1]);
  // AND_Gate and_15: pin names not known; wires that end beside it: Number_to_display[2], Number_to_display[3], and_15_p3
  // NOT_Gate not_19: pin names not known; wires that end beside it: Number_to_display[2]
  // NOT_Gate not_20: pin names not known; wires that end beside it: Number_to_display[3]
  // NOT_Gate not_21: pin names not known; wires that end beside it: Number_to_display[0], not_21_p2
  // NOT_Gate not_22 has open pins: in=Number_to_display[1], out=open
  // NOT_Gate not_23: pin names not known; wires that end beside it: Number_to_display[2], not_23_p2
  // NOT_Gate not_24: pin names not known; wires that end beside it: Number_to_display[3]
  or or_10 (or_10_out, and_11_out, and_12_out);
  or or_11 (or_11_out, and_13_p3, Number_to_display[3]);
  and and_16 (and_16_out, not_21_p2, Number_to_display[1]);
  or or_12 (d7, and_16_out, and_17_out);
  and and_17 (and_17_out, not_21_p2, not_23_p2);
  or or_13 (d1, or_10_out, or_11_out);
  or or_14 (d4, and_14_out, and_14_out);
  _7_Segment_Display u_7_segment_display_1 (.g(d0), .f(d1), .a(d2), .b(d3), .e(d7), .d(d6), .c(d5), .dp(d4));
  // NOT_Gate not_25: pin names not known; wires that end beside it: Number_to_display[0], not_25_p2
  // NOT_Gate not_26 has open pins: in=Number_to_display[1], out=open
  // NOT_Gate not_27: pin names not known; wires that end beside it: Number_to_display[2], not_27_p2
  // NOT_Gate not_28: pin names not known; wires that end beside it: Number_to_display[3]
  // NOT_Gate not_29: pin names not known; wires that end beside it: Number_to_display[0]
  not not_30 (not_30_out, Number_to_display[1]);
  // NOT_Gate not_31: pin names not known; wires that end beside it: Number_to_display[2]
  // NOT_Gate not_32: pin names not known; wires that end beside it: Number_to_display[3]
  // AND_Gate and_18: pin names not known; wires that end beside it: Number_to_display[0], Number_to_display[2], and_18_p3
  or or_15 (or_15_out, and_18_p3, and_19_p4);
  // AND_Gate and_19: pin names not known; wires that end beside it: not_25_p2, not_25_p2, not_27_p2, and_19_p4
  or or_16 (or_16_out, Number_to_display[3], Number_to_display[1]);
  or or_17 (or_17_out, Number_to_display[0], not_30_out, not_30_out);
  or or_18 (d2, or_15_out, or_16_out);
  or or_19 (d5, or_17_out, Number_to_display[2]);

  // Other names for the same wires on the sheet: number[3:0] = Number_to_display;
  //   segments[7:0] = Segment_configuration

  // Notes on the sheet:
  //   These are the inputs
  //   of your circuit.
  //   Do not modify this!
  //   Put your name and id here: Xirui Ren - xir19
  //   contents of rom_1 (hex, n*v repeats v):
  //   ee 28 cd 6d 2b 67 e7 2c ef 6f f6 23 d5 5e e5 34
  //   This is not a valid solution! Solve this with gates!
  //   If you submit this, the autograder will give you 100%
  //   But you will still get a zero
  //   These are the outputs
  //   of your circuit.
  //   Do not modify this!
endmodule
