// Logisim project ALU.circ as structural Verilog: 4 circuits, main circuit main
module main (
  input  [2:0] ALUOp,
  input  [15:0] A,
  input  [15:0] B,
  input  in_4,
  output [15:0] Result,
  output [15:0] HI,
  output [15:0] LO,
  output GT,
  output Zero,
  output LT
);

  wire [15:0] _000, _001, _010, _011, _110, _111, DIV_hi, DIV_lo, MUL_hi, MUL_lo, multiplexer_1_out,
       multiplexer_2_out;

  assign _000 = ~(A & B);  // NAND_Gate NAND, 16 bits wide
  MUL MUL (.A(A), .B(B), .HI(MUL_hi), .LO(MUL_lo));
  DIV DIV (.A(A), .B(B), .HI(DIV_hi), .LO(DIV_lo));
  Multiplexer #(.select(3), .width(16)) multiplexer_1 (
    .in4(MUL_hi), .in5(DIV_hi), .out(multiplexer_1_out), .sel(ALUOp));  // open: in0, in1, in2, in3, in6, in7, en
  Multiplexer #(.select(3), .width(16)) multiplexer_2 (
    .in4(MUL_lo), .in5(DIV_lo), .out(multiplexer_2_out), .sel(ALUOp));  // open: in0, in1, in2, in3, in6, in7, en
  Register #(.width(16)) register_1 (.D(multiplexer_1_out), .en(1'b1), .Q(HI), .clk(in_4));  // open: clr
  Register #(.width(16)) register_2 (.D(multiplexer_2_out), .en(1'b1), .Q(LO), .clk(in_4));  // open: clr
  assign _001 = A | B;  // OR_Gate OR, 16 bits wide
  Multiplexer #(.select(3), .width(16)) multiplexer_3 (
    .in0(_000), .in1(_001), .in2(_010), .in3(_011), .in4({16{1'b0}}), .in5({16{1'b0}}), .in6(_110),
    .in7(_111), .out(Result), .sel(ALUOp));  // open: en
  Adder #(.width(16)) adder_1 (.a(A), .b(B), .out(_010));  // open: cin, cout
  Subtractor #(.width(16)) subtractor_1 (.a(A), .b(B), .out(_011));  // open: bin, bout
  Comparator #(.width(16)) comparator_1 (.a(A), .b({16{1'b0}}), .gt(GT), .eq(Zero), .lt(LT));
  Shifter #(.width(16)) shifter_1 (.in(A), .\dist (B[3:0]), .out(_110));
  Shifter #(.width(16), .shift("lr")) shifter_2 (.in(A), .\dist (B[3:0]), .out(_111));

  // Other names for the same wires on the sheet: Clock = in_4

  // Notes on the sheet:
  //   Inputs
  //   Design your ALU in this file
  //   A - First ALU input
  //   B - Second ALU input
  //   Result - ALU main result
  //   HI/LO the value of the ALU registers using for mul/div
  //   GT/Zero/LT - Comparison of input A with zero
  //   ALUOp - The control signal defining the behaviour of the ALU
  //   Xirui Ren - xir19
  //   Outputs
endmodule

module test (
  input  [2:0] in_1,
  input  [15:0] in_2,
  input  [15:0] in_3
);

  wire button_1_out, main_1_gt, main_1_lt, main_1_zero;
  wire [15:0] main_1_hi, main_1_lo, main_1_result;

  main main_1 (
    .ALUOp(in_1), .A(in_2), .B(in_3), .Result(main_1_result), .GT(main_1_gt), .Zero(main_1_zero),
    .LT(main_1_lt), .in_4(button_1_out), .HI(main_1_hi), .LO(main_1_lo));
  Button button_1 (.out(button_1_out));
  // Probe on main_1_result
  // Probe on main_1_hi
  // Probe on main_1_lo
  // Probe on main_1_gt
  // Probe on main_1_zero
  // Probe on main_1_lt

  // Notes on the sheet:
  //   Test your circuit!
endmodule

module MUL (
  input  [15:0] A,
  input  [15:0] B,
  output [15:0] HI,
  output [15:0] LO
);

  Multiplier #(.width(16)) multiplier_1 (.a(A), .b(B), .out(LO), .cout(HI));  // open: cin
endmodule

module DIV (
  input  [15:0] A,
  input  [15:0] B,
  output [15:0] HI,
  output [15:0] LO
);

  Divider #(.width(16)) divider_1 (.a(A), .b(B), .out(LO), .rem(HI));  // open: upper
endmodule
