// Logisim project umips.circ as structural Verilog: 3 circuits, main circuit main
module main (
  output [15:0] Reg0,
  output [15:0] Reg1,
  output [15:0] Reg2,
  output [15:0] Reg3,
  output [15:0] Reg4,
  output [15:0] Reg5,
  output [15:0] Reg6,
  output [15:0] Reg7,
  output [3:0] Output3,
  output [3:0] Output2,
  output [3:0] Output1,
  output [3:0] Output0,
  output halt
);

  wire bn, bnF, bnT, bp, bpF, bpT, branch, branT, bx, bxF, bxT, bz, bzF, bzT, clock, comparator_1_gt,
       comparator_1_lt, demultiplexer_1_out1, demultiplexer_2_out1, demultiplexer_3_out1,
       demultiplexer_4_out1, field_1_subop, GT, immInv, j, jal, jr, li, LT, lw, mfhi, mflo, \nand ,
       not_1_out, not_2_out, or_1_out, or_2_out, or_4_out, or_5_out, put, RegWrite, sw, Z;
  wire [1:0] ALUSur, BJ;
  wire [2:0] ALUOp, field_1_rs, field_1_rt, writeWhat;
  wire [3:0] field_1_opcode;
  wire [7:0] bit_extender_1_out, bit_extender_2_out, Imm, multiplexer_1_out, multiplexer_4_out, PC_1, PC_q;
  wire [15:0] and_1_out, and_6_out, Hi, lo, main_1_readdata1, main_2_result, multiplexer_2_out,
       multiplexer_3_out, PC_1_Reg, ram_1_data, rom_1_data, RSdata, SignedImm, ZeroImm;

  LED led_1 (.in(halt));
  Register #(.width(16)) RS (.D(RSdata), .en(put), .Q({Output3, Output2, Output1, Output0}), .clk(clock));  // open: clr
  Comparator #(.width(3)) comparator_1 (.a(ALUOp), .b(3'b000), .gt(comparator_1_gt), .lt(comparator_1_lt));  // open: eq
  assign and_1_out = RSdata & 16'hff;  // AND_Gate and_1, 16 bits wide
  Demultiplexer demultiplexer_1 (.out0(bnF), .out1(demultiplexer_1_out1), .in(branch), .sel(LT));  // open: en
  Adder adder_1 (.a(PC_q), .b(8'h1), .out(PC_1));  // open: cin, cout
  Bit_Extender #(.in_width(16), .out_width(8)) bit_extender_1 (.in(and_1_out), .out(bit_extender_1_out));
  Clock clock_1 (.out(clock));
  or or_1 (or_1_out, j, jal);
  and and_2 (bnT, demultiplexer_1_out1, bn);
  Hex_Digit_Display hex_digit_display_1 (.value(Output3));  // open: dp
  or or_2 (or_2_out, comparator_1_gt, comparator_1_lt);
  Multiplexer #(.select(2), .width(8)) multiplexer_1 (
    .in0(PC_1), .in1(Imm), .in2(Imm), .in3(bit_extender_1_out), .out(multiplexer_1_out), .sel(BJ));  // open: en
  Priority_Encoder #(.select(2)) priority_encoder_1 (
    .in0(1'b1), .in1(branT), .in2(or_1_out), .in3(jr), .out(BJ));  // open: gs, en_out, en_in
  or or_3 (branT, bpT, bnT, bzT, bxT);
  Hex_Digit_Display hex_digit_display_2 (.value(Output1));  // open: dp
  Hex_Digit_Display hex_digit_display_3 (.value(Output2));  // open: dp
  Priority_Encoder priority_encoder_2 (
    .in0(\nand ), .in2(or_2_out), .in3(li), .in4(mflo), .in5(lw), .in6(mfhi), .in7(jal), .out(writeWhat));  // open: in1, en_in, gs, en_out
  Register PC (.D(multiplexer_1_out), .en(not_1_out), .Q(PC_q), .clk(clock));  // open: clr
  not not_1 (not_1_out, halt);
  Demultiplexer demultiplexer_2 (.out0(bpF), .out1(demultiplexer_2_out1), .in(branch), .sel(GT));  // open: en
  Hex_Digit_Display hex_digit_display_4 (.value(Output0));  // open: dp
  and and_3 (bpT, demultiplexer_2_out1, bp);
  ROM #(.dataWidth(16)) rom_1 (.addr(PC_q), .data(rom_1_data));  // open: sel
  Demultiplexer demultiplexer_3 (.out0(bzF), .out1(demultiplexer_3_out1), .in(branch), .sel(Z));  // open: en
  field field_1 (
    .Instruction(rom_1_data), .Opcode(field_1_opcode), .Rs(field_1_rs), .Rt(field_1_rt), .Immediate(Imm),
    .Subop(field_1_subop));  // open: Unused
  and and_4 (bzT, demultiplexer_3_out1, bz);
  control control_1 (
    .SubOp(field_1_subop), .Opcode(field_1_opcode), .ALUOp(ALUOp), .ALUSor(ALUSur), .bz(bz), .bp(bp),
    .jal(jal), .bn(bn), .jr(jr), .j(j), .bx(bx), .WriteMem(sw), .MemRead(lw), .mfhi(mfhi), .halt(halt),
    .li(li), .mflo(mflo), .put(put), .RegWrite(RegWrite), .Branch(branch), .immInvo(immInv), .\nand (\nand ));
  Demultiplexer demultiplexer_4 (.out0(bxF), .out1(demultiplexer_4_out1), .in(branch), .sel(or_4_out));  // open: en
  or or_4 (or_4_out, LT, GT);
  Multiplexer #(.select(3), .width(16)) multiplexer_2 (
    .in0(main_2_result), .in2(main_2_result), .in3(ZeroImm), .in4(lo), .in5(ram_1_data), .in6(Hi),
    .in7(PC_1_Reg), .out(multiplexer_2_out), .sel(writeWhat));  // open: in1, en
  and and_5 (bxT, demultiplexer_4_out1, bx);
  RegFile_main main_1 (
    .ReadData0(RSdata), .ReadData1(main_1_readdata1), .Reg0(Reg0), .Reg1(Reg1), .Reg2(Reg2), .Reg3(Reg3),
    .Reg4(Reg4), .Reg5(Reg5), .Reg6(Reg6), .Reg7(Reg7), .WriteData0(multiplexer_2_out),
    .WriteSelect0(field_1_rs), .ReadSelect0(field_1_rs), .ReadSelect1(field_1_rt), .WE0(RegWrite),
    .Clock(clock));
  Multiplexer #(.select(2), .width(16)) multiplexer_3 (
    .in0(main_1_readdata1), .in1(ZeroImm), .in2(SignedImm), .in3(main_1_readdata1), .out(multiplexer_3_out),
    .sel(ALUSur));  // open: en
  assign and_6_out = main_1_readdata1 & 16'hff;  // AND_Gate and_6, 16 bits wide
  ALU_main main_2 (
    .ALUOp(ALUOp), .A(RSdata), .B(multiplexer_3_out), .Result(main_2_result), .GT(GT), .Zero(Z), .LT(LT),
    .in_4(clock), .HI(Hi), .LO(lo));
  Bit_Extender #(.in_width(16), .out_width(8)) bit_extender_2 (.in(and_6_out), .out(bit_extender_2_out));
  Multiplexer #(.width(8)) multiplexer_4 (
    .in0(bit_extender_2_out), .in1(PC_1), .out(multiplexer_4_out), .sel(not_2_out));  // open: en
  not not_2 (not_2_out, or_5_out);
  or or_5 (or_5_out, sw, lw);
  assign ZeroImm = {{8{1'b0}}, Imm};  // Bit_Extender bit_extender_3
  assign PC_1_Reg = {{8{1'b0}}, PC_1};  // Bit_Extender bit_extender_4
  assign SignedImm = {{8{Imm[7]}}, Imm};  // Bit_Extender bit_extender_5
  RAM #(.dataWidth(16), .bus("separate")) ram_1 (
    .addr(multiplexer_4_out), .din(RSdata), .data(ram_1_data), .str(sw), .clk(clock));  // open: sel, ld, clr
  // RegFile_main main_3: pin names not known
  // ALU_main main_4: pin names not known

  // Notes on the sheet:
  //   Xirui Ren - xir19
  //   Connect Output3..0 to your LED display.
  //   Output3 is the most significant
  //   Connect halt to your halt LED
  //   May need to restart Logisim
  //   If you change them in there, changes will be reflected here!
  //   There circuits are in the other 2 files I gave you... I've imported them to this file
endmodule

module control (
  input  SubOp,
  input  [3:0] Opcode,
  output [2:0] ALUOp,
  output [1:0] ALUSor,
  output bz,
  output bp,
  output jal,
  output bn,
  output jr,
  output j,
  output bx,
  output WriteMem,
  output MemRead,
  output mfhi,
  output halt,
  output li,
  output mflo,
  output put,
  output RegWrite,
  output Branch,
  output immInvo,
  output \nand 
);

  wire add, addi, addui, decoder_1_out0, decoder_1_out1, decoder_1_out2, decoder_1_out3, decoder_1_out4,
       decoder_1_out5, decoder_1_out6, decoder_1_out7, decoder_1_out8, decoder_1_out9, decoder_1_out10,
       decoder_1_out12, decoder_1_out13, decoder_1_out14, div, mul, \or , or_4_out, sllv, srlv, sub;

  Decoder #(.select(4)) decoder_1 (
    .out0(decoder_1_out0), .out1(decoder_1_out1), .out2(decoder_1_out2), .out3(decoder_1_out3),
    .out4(decoder_1_out4), .out5(decoder_1_out5), .out6(decoder_1_out6), .out7(decoder_1_out7),
    .out8(decoder_1_out8), .out9(decoder_1_out9), .out10(decoder_1_out10), .out11(put),
    .out12(decoder_1_out12), .out13(decoder_1_out13), .out14(decoder_1_out14), .out15(halt), .sel(Opcode));  // open: en
  or or_1 (Branch, bz, bp, bn, bx);
  Demultiplexer demultiplexer_1 (.out0(add), .out1(addui), .in(decoder_1_out0), .sel(SubOp));  // open: en
  Demultiplexer demultiplexer_2 (.out0(sub), .out1(jal), .in(decoder_1_out8), .sel(SubOp), .en(SubOp));
  Demultiplexer demultiplexer_3 (.out0(\or ), .in(decoder_1_out12), .sel(SubOp));  // open: out1, en
  or or_2 (immInvo, addui, addi, j, jal, bz, bp, bn, bx);
  Demultiplexer demultiplexer_4 (.out0(\nand ), .out1(bn), .in(decoder_1_out4), .sel(SubOp));  // open: en
  Demultiplexer demultiplexer_5 (.out0(mflo), .out1(addi), .in(decoder_1_out1), .sel(SubOp));  // open: en
  Demultiplexer demultiplexer_6 (.out0(mul), .in(decoder_1_out10), .sel(SubOp));  // open: out1, en
  Demultiplexer demultiplexer_7 (.out0(sllv), .in(decoder_1_out14), .sel(SubOp));  // open: out1, en
  Demultiplexer demultiplexer_8 (.out0(WriteMem), .in(decoder_1_out13), .sel(SubOp));  // open: out1, en
  Demultiplexer demultiplexer_9 (.out0(div), .out1(li), .in(decoder_1_out2), .sel(SubOp));  // open: en
  Demultiplexer demultiplexer_10 (.out0(MemRead), .out1(bx), .in(decoder_1_out5), .sel(SubOp));  // open: en
  Demultiplexer demultiplexer_11 (.out0(srlv), .out1(bz), .in(decoder_1_out6), .sel(SubOp));  // open: en
  Demultiplexer demultiplexer_12 (.out0(mfhi), .out1(j), .in(decoder_1_out9), .sel(SubOp));  // open: en
  Demultiplexer demultiplexer_13 (.out1(jr), .in(decoder_1_out7), .sel(SubOp));  // open: out0, en
  or or_3 (RegWrite, add, addui, addi, \nand , \or , sllv, srlv, mfhi, mflo, li, MemRead, jal, sub);
  Demultiplexer demultiplexer_14 (.out1(bp), .in(decoder_1_out3), .sel(SubOp));  // open: out0, en
  or or_4 (or_4_out, add, addui, addi);
  Priority_Encoder priority_encoder_1 (
    .in0(1'b1), .in1(\or ), .in2(or_4_out), .in3(sub), .in4(mul), .in5(div), .in6(sllv), .in7(srlv),
    .out(ALUOp));  // open: en_in, gs, en_out
  Priority_Encoder #(.select(2)) priority_encoder_2 (
    .in0(1'b1), .in1(addui), .in2(addi), .out(ALUSor));  // open: in3, gs, en_out, en_in

  // Other names for the same wires on the sheet: lw = MemRead; sw = WriteMem
endmodule

// Fields
module field (
  input  [15:0] Instruction,
  output [3:0] Opcode,
  output [2:0] Rs,
  output [2:0] Rt,
  output [4:0] Unused,
  output [7:0] Immediate,
  output Subop
);

  wire [15:0] shifter_1_out;
  wire [15:8] and_1_out;

  Shifter #(.width(16), .shift("lr")) shifter_1 (.in(Instruction), .\dist (4'b0001), .out(shifter_1_out));
  assign {and_1_out, Immediate} = shifter_1_out & 16'hff;  // AND_Gate and_1, 16 bits wide

  assign Opcode = Instruction[15:12];
  assign Rs = Instruction[11:9];
  assign Rt = Instruction[8:6];
  assign Subop = Instruction[0];
  assign Unused = Instruction[5:1];

  // Other names for the same wires on the sheet: Imm[7:0] = Immediate; Uns[4:0] = Instruction[5:1];
  //   Opc[3:0] = Instruction[15:12]
endmodule
