// Logisim project lab12C.circ as structural Verilog: 1 circuit, main circuit main
module main (
  input  Bit,
  input  Clock,
  output Output
);


  assign Output = Bit;

  // Notes on the sheet:
  //   of your circuit.
  //   These are the inputs
  //   Do not modify this!
  //   These are the outputs
  //   of your circuit.
  //   Do not modify this!
endmodule
